// Digital circuit circuito.dig as structural Verilog
module circuito (
  input  clk1,
  input  btn,
  output E0S1,
  output E1S1,
  output ES2,
  output E0S3,
  output E1S3,
  output ES4
);

  wire and_1_out, and_2_out, and_3_out, and_4_out, and_5_out, and_6_out, and_7_out, and_8_out, and_9_out,
       and_10_out, and_11_out, and_12_out, E1_nq, E1_q, E2_nq, E2_q, E3_nq, E3_q, E4_nq, not_1_out, or_1_out,
       or_2_out, or_3_out;

  D_FF E1 (.D(and_1_out), .C(clk1), .Q(E1_q), .nQ(E1_nq));
  D_FF E2 (.D(or_1_out), .C(clk1), .Q(E2_q), .nQ(E2_nq));
  D_FF E3 (.D(or_2_out), .C(clk1), .Q(E3_q), .nQ(E3_nq));
  D_FF E4 (.D(or_3_out), .C(clk1), .Q(E3_nq), .nQ(E4_nq));
  and and_1 (and_1_out, btn, E3_nq, E3_q, E2_nq, E1_nq);
  and and_2 (and_2_out, btn, E3_nq, E1_nq);
  and and_3 (and_3_out, E3_nq, E3_nq, E2_q, E1_nq);
  or or_1 (or_1_out, and_5_out, and_4_out, and_3_out, and_2_out);
  and and_4 (and_4_out, E3_nq, E3_q, E2_nq, E1_nq);
  and and_5 (and_5_out, E4_nq, E3_nq);
  not not_1 (not_1_out, btn);
  and and_6 (and_6_out, btn, E3_nq);
  and and_7 (and_7_out, not_1_out, E3_nq, E3_nq);
  or or_2 (or_2_out, and_8_out, and_7_out, and_6_out, E1_q);
  and and_8 (and_8_out, E4_nq, E3_q);
  and and_9 (and_9_out, E4_nq, E3_q);
  and and_10 (and_10_out, btn, E4_nq, E3_nq);
  or or_3 (or_3_out, and_12_out, and_11_out, and_10_out, and_9_out, E1_q);
  and and_11 (and_11_out, E4_nq, E3_nq, E2_nq, E1_nq);
  and and_12 (and_12_out, btn, E3_nq, E2_nq, E1_nq);
endmodule
